// Logisim project latch_sr.circ as structural Verilog: 1 circuit, main circuit main
module latch_sr (
);

  wire nor_1_out, nor_2_out, R_out, S_out;

  Button R (.out(R_out));
  Button S (.out(S_out));
  // NOR_Gate nor_1 has open pins: out=nor_1_out
  // NOR_Gate nor_2 has open pins: out=nor_2_out
  LED Q (.in(nor_1_out));
  LED Qn (.in(nor_2_out));
endmodule
