// Logisim project meia_somadora.circ as structural Verilog: 1 circuit, main circuit main
module meia_somadora (
  input  A,
  input  B,
  output S,
  output C
);

  // XOR_Gate xor_1 has open pins: out=S
  // AND_Gate and_1 has open pins: out=C
endmodule
