// Logisim project pisca_clock.circ as structural Verilog: 1 circuit, main circuit main
module pisca_pisca (
);

  wire CLK_out, not_1_out, undriven;

  Clock CLK (.out(CLK_out));
  not not_1 (not_1_out, CLK_out);
  LED LED (.in(not_1_out));
  LED CLK_direto (.in(undriven));
endmodule
